# Fritzing sketch ephysSuiteSetup (saved by Fritzing 0.9.3b)
breadboards: 1

parts:
  Part1 = Arduino Uno (Rev3)
  R1 = Resistor [tolerance=±5% resistance=220 package=THT]
  R2 = Resistor [tolerance=±5% resistance=220 package=THT]
  J2 = Screw terminal - 2 pins [package=THT]
  Part3 = TRRS 3.5mm Jack Breakout
  MIC1 = MAX4466_Electret_Microphone_Breakout_Board
  J3 = Screw terminal - 2 pins [package=THT]
  R3 = Resistor [tolerance=±5% resistance=220 package=THT]
  R4 = Resistor [tolerance=±5% resistance=220 package=THT]  # not connected
  R5 = Resistor [tolerance=±5% resistance=220 package=THT]

nets:
  N1: Part1.GND, R2.Pin_0, Part3.TIP, MIC1.connector2, R5.Pin_0
  N2: Part1.D6_PWM, R1.Pin_1
  N3: Part1.5V, MIC1.connector3
  N4: R1.Pin_0, R2.Pin_1, J2.pin2
  N5: MIC1.connector1, R3.Pin_1
  N6: J3.pin1, R3.Pin_0, R5.Pin_1

notes:
  Channel 2
  Channel 1
  Intan RHD2000 evaluation board analog ports
  Channel 4
  Channel 3
  Adafruit MAX 4466 Electret Microphone
  3.5 mm audio cable from computer split between audio breakout board and speaker
