# Fritzing sketch ephysSuiteSetup (saved by Fritzing 0.9.4)
breadboards: 1

parts:
  Part1 = Arduino Uno (Rev3)
  R1 = Resistor [tolerance=±5% resistance=220 package=THT]
  R2 = Resistor [tolerance=±5% resistance=220 package=THT]
  J2 = Screw terminal - 2 pins [package=THT]
  Part3 = TRRS 3.5mm Jack Breakout
  MIC1 = MAX4466 Electret Microphone Breakout Board
  J3 = Screw terminal - 2 pins [package=THT]
  R3 = Resistor [tolerance=±5% resistance=220 package=THT]
  R5 = Resistor [tolerance=±5% resistance=220 package=THT]
  C1 = Tantalum Capacitor [capacitance=1μF package="100 mil [THT, tantalum]"]

nets:
  GND: Part1.GND, R2.Pin_0, Part3.TIP, MIC1.GND, R3.Pin_1
  N1: Part1.D6_PWM, R1.Pin_1
  N2: Part1.5V, R5.Pin_0
  N3: R1.Pin_0, R2.Pin_1, J2.pin2
  N4: J2.pin1, C1.-
  N5: Part3.SLEEVE, C1.+
  N6: MIC1.out, J3.pin2
  N7: MIC1.VCC, R3.Pin_0, R5.Pin_1

notes:
  Channel 2
  Channel 1
  Intan RHD2000 evaluation board analog ports
  Channel 8
  ...                         Channel 7
  Adafruit MAX 4466 Electret Microphone
  3.5 mm audio cable from computer split between audio breakout board and speaker

custom parts:
  MAX4466 Electret Microphone Breakout Board: MAX4466 Electrec Microphone Breakout Board
